// Digital circuit P8D16A_2A main.dig as structural Verilog
module P8D16A_2A_main (
  input  CLK
);

  wire A_o0, A_o1, A_o2, A_o3, A_o4, A_o5, A_o6, A_o7, alu_1_f0, alu_1_fc, alu_1_fn, alu_1_fo, alu_1_o0,
       alu_1_o1, alu_1_o2, alu_1_o3, alu_1_o4, alu_1_o5, alu_1_o6, alu_1_o7, AO0, AO1, AO2, AO3, AO4, AO5,
       AO6, AO7, clock_1_clk, fumemory16_1_o0, fumemory16_1_o1, fumemory16_1_o2, fumemory16_1_o3,
       fumemory16_1_o4, fumemory16_1_o5, fumemory16_1_o6, fumemory16_1_o7, instruction_decoder_1_p1,
       instruction_decoder_1_p10, instruction_decoder_1_p11, mareg16b_1_o0, mareg16b_1_o1, mareg16b_1_o2,
       mareg16b_1_o3, mareg16b_1_o4, mareg16b_1_o5, mareg16b_1_o6, mareg16b_1_o7, mareg16b_1_o8,
       mareg16b_1_o9, mareg16b_1_o10, mareg16b_1_o11, mareg16b_1_o12, mareg16b_1_o13, mareg16b_1_o14,
       mareg16b_1_o15, undriven, undriven_2, undriven_3, undriven_4, undriven_5, undriven_6, undriven_7,
       undriven_8, undriven_9, undriven_10, undriven_11, undriven_12, undriven_13, undriven_14, undriven_15,
       undriven_16, undriven_17, undriven_18, undriven_19, undriven_20, undriven_21, undriven_22,
       undriven_23, undriven_24, undriven_25, undriven_26, undriven_27, undriven_28, undriven_29,
       undriven_30, undriven_31, undriven_32, undriven_33, undriven_34, undriven_35, undriven_36,
       undriven_37, undriven_38, undriven_39, undriven_40, undriven_41, undriven_42, undriven_43,
       undriven_44, undriven_45, undriven_46, undriven_47, undriven_48, undriven_49, undriven_50,
       undriven_51, undriven_52, undriven_53, undriven_54, undriven_55, undriven_56, undriven_57,
       undriven_58, undriven_59, undriven_60, undriven_61, undriven_62, undriven_63, undriven_64,
       undriven_65, undriven_66, X_o0, X_o1, X_o2, X_o3, X_o4, X_o5, X_o6, X_o7;

  Register A (
    .CLK(undriven_63), .E(undriven_64), .R(1'b1), .W(undriven_66), .D0(X_o0), .D1(X_o1), .D2(X_o2),
    .D3(X_o3), .D4(X_o4), .D5(X_o5), .D6(X_o6), .D7(X_o7), .O0(A_o0), .O1(A_o1), .O2(A_o2), .O3(A_o3),
    .O4(A_o4), .O5(A_o5), .O6(A_o6), .O7(A_o7));
  Register X (
    .CLK(undriven_47), .E(undriven_50), .R(undriven_53), .W(undriven_62), .D0(X_o0), .D1(X_o1), .D2(X_o2),
    .D3(X_o3), .D4(X_o4), .D5(X_o5), .D6(X_o6), .D7(X_o7), .O0(X_o0), .O1(X_o1), .O2(X_o2), .O3(X_o3),
    .O4(X_o4), .O5(X_o5), .O6(X_o6), .O7(X_o7));
  Clock clock_1 (.HLT(undriven_52), .Clock(CLK), .M_CLK(1'b0), .M_E(1'b0), .CLK(clock_1_clk));
  PinControl8b pincontrol8b_1 (
    .E(undriven_65), .D0(A_o0), .D1(A_o1), .D2(A_o2), .D3(A_o3), .D4(A_o4), .D5(A_o5), .D6(A_o6), .D7(A_o7),
    .O0(X_o0), .O1(X_o1), .O2(X_o2), .O3(X_o3), .O4(X_o4), .O5(X_o5), .O6(X_o6), .O7(X_o7));
  ALU alu_1 (
    .A0(AO0), .A1(AO1), .A2(AO2), .A3(AO3), .A4(AO4), .A5(AO5), .A6(AO6), .A7(AO7), .B0(undriven_54),
    .B1(undriven_55), .B2(undriven_56), .B3(undriven_57), .B4(undriven_58), .B5(undriven_59),
    .B6(undriven_60), .B7(undriven_61), .B(undriven_36), .C(undriven_37), .S(undriven_38), .AND(undriven_39),
    .ADD(undriven_40), .OR(undriven_41), .NOT(undriven_42), .XOR(undriven_43), .SL(undriven_44),
    .SR(undriven_45), .RL(undriven_46), .RR(undriven_48), .MULT(undriven_49), .DIV(undriven_51),
    .O0(alu_1_o0), .O1(alu_1_o1), .O2(alu_1_o2), .O3(alu_1_o3), .O4(alu_1_o4), .O5(alu_1_o5), .O6(alu_1_o6),
    .O7(alu_1_o7), .F0(alu_1_f0), .FN(alu_1_fn), .FC(alu_1_fc), .FO(alu_1_fo));  // open: E
  StackPointer SP (
    .CLK(undriven_27), .INC(undriven_29), .DEC(undriven_31), .R(undriven_33), .W(undriven_35), .D0(X_o0),
    .D1(X_o1), .D2(X_o2), .D3(X_o3), .D4(X_o4), .D5(X_o5), .D6(X_o6), .D7(X_o7), .O0(X_o0), .O1(X_o1),
    .O2(X_o2), .O3(X_o3), .O4(X_o4), .O5(X_o5), .O6(X_o6), .O7(X_o7));
  Register Y (
    .CLK(undriven_28), .E(undriven_30), .R(undriven_32), .W(undriven_34), .D0(X_o0), .D1(X_o1), .D2(X_o2),
    .D3(X_o3), .D4(X_o4), .D5(X_o5), .D6(X_o6), .D7(X_o7), .O0(X_o0), .O1(X_o1), .O2(X_o2), .O3(X_o3),
    .O4(X_o4), .O5(X_o5), .O6(X_o6), .O7(X_o7));
  Register Z (
    .CLK(undriven_9), .E(undriven_6), .R(undriven_4), .W(undriven_2), .D0(X_o0), .D1(X_o1), .D2(X_o2),
    .D3(X_o3), .D4(X_o4), .D5(X_o5), .D6(X_o6), .D7(X_o7), .O0(X_o0), .O1(X_o1), .O2(X_o2), .O3(X_o3),
    .O4(X_o4), .O5(X_o5), .O6(X_o6), .O7(X_o7));
  Reg16 O (
    .CLK(undriven_10), .E(undriven_8), .R(undriven_7), .W(undriven_5), .D0(undriven_3), .D1(undriven),
    .D2(X_o0), .D3(X_o1), .D4(X_o2), .D5(X_o3), .D6(X_o4), .D7(X_o5), .D8(X_o6), .D9(X_o7), .O0(X_o0),
    .O1(X_o1), .O2(X_o2), .O3(X_o3), .O4(X_o4), .O5(X_o5), .O6(X_o6), .O7(X_o7));  // open: D10, D11, D12, D13, D14, D15, O8, O9, O10, O11, O12, O13, O14, O15
  ProgramCounter PC (
    .CLK(undriven_19), .E(undriven_16), .R(undriven_14), .W(undriven_12), .D0(X_o0), .D1(X_o1), .D2(X_o2),
    .D3(X_o3), .D4(X_o4), .D5(X_o5), .D6(X_o6), .D7(X_o7), .O0(X_o0), .O1(X_o1), .O2(X_o2), .O3(X_o3),
    .O4(X_o4), .O5(X_o5), .O6(X_o6), .O7(X_o7));
  ProgramCounter16 programcounter16_1 (
    .CLK(undriven_20), .E(undriven_18), .RL(undriven_17), .WL(undriven_15), .RH(undriven_13),
    .WH(undriven_11), .D0(X_o0), .D1(X_o1), .D2(X_o2), .D3(X_o3), .D4(X_o4), .D5(X_o5), .D6(X_o6), .D7(X_o7),
    .O0(X_o0), .O1(X_o1), .O2(X_o2), .O3(X_o3), .O4(X_o4), .O5(X_o5), .O6(X_o6), .O7(X_o7));
  // Instruction_Decoder instruction_decoder_1: pin names not known; wires that end beside it: instruction_decoder_1_p1, X_o0, X_o1, X_o2, X_o3, X_o4, X_o5, X_o6, X_o7, instruction_decoder_1_p10, instruction_decoder_1_p11, X_o5, X_o6, X_o7
  MAReg16b mareg16b_1 (
    .CLK(undriven_24), .E(undriven_23), .WL(undriven_22), .WH(undriven_21), .D0(fumemory16_1_o0),
    .D1(fumemory16_1_o1), .D2(fumemory16_1_o2), .D3(fumemory16_1_o3), .D4(fumemory16_1_o4),
    .D5(fumemory16_1_o5), .D6(fumemory16_1_o6), .D7(fumemory16_1_o7), .O0(mareg16b_1_o0), .O1(mareg16b_1_o1),
    .O2(mareg16b_1_o2), .O3(mareg16b_1_o3), .O4(mareg16b_1_o4), .O5(mareg16b_1_o5), .O6(mareg16b_1_o6),
    .O7(mareg16b_1_o7), .O8(mareg16b_1_o8), .O9(mareg16b_1_o9), .O10(mareg16b_1_o10), .O11(mareg16b_1_o11),
    .O12(mareg16b_1_o12), .O13(mareg16b_1_o13), .O14(mareg16b_1_o14), .O15(mareg16b_1_o15));
  FUMemory16 fumemory16_1 (
    .CLK(undriven_24), .R(undriven_26), .W(undriven_25), .A0(mareg16b_1_o0), .A1(mareg16b_1_o1),
    .A2(mareg16b_1_o2), .A3(mareg16b_1_o3), .A4(mareg16b_1_o4), .A5(mareg16b_1_o5), .A6(mareg16b_1_o6),
    .A7(mareg16b_1_o7), .A8(mareg16b_1_o8), .A9(mareg16b_1_o9), .A10(mareg16b_1_o10), .A11(mareg16b_1_o11),
    .A12(mareg16b_1_o12), .A13(mareg16b_1_o13), .A14(mareg16b_1_o14), .A15(mareg16b_1_o15),
    .D0(fumemory16_1_o0), .D1(fumemory16_1_o1), .D2(fumemory16_1_o2), .D3(fumemory16_1_o3),
    .D4(fumemory16_1_o4), .D5(fumemory16_1_o5), .D6(fumemory16_1_o6), .D7(fumemory16_1_o7),
    .O0(fumemory16_1_o0), .O1(fumemory16_1_o1), .O2(fumemory16_1_o2), .O3(fumemory16_1_o3),
    .O4(fumemory16_1_o4), .O5(fumemory16_1_o5), .O6(fumemory16_1_o6), .O7(fumemory16_1_o7));  // open: E
endmodule
