// Digital circuit Adder8b.dig as structural Verilog
module Adder8b (
  input  E,
  input  X0,
  input  X1,
  input  X2,
  input  X3,
  input  X4,
  input  X5,
  input  X6,
  input  X7,
  input  Y0,
  input  Y1,
  input  Y2,
  input  Y3,
  input  Y4,
  input  Y5,
  input  Y6,
  input  Y7,
  input  C,
  input  S,
  output O0,
  output O1,
  output O2,
  output O3,
  output O4,
  output O5,
  output O6,
  output O7,
  output CO,
  output OO
);

  wire and_1_out, and_2_out, full_adder_1_co, full_adder_1_s, full_adder_2_co, full_adder_2_s,
       full_adder_3_co, full_adder_3_s, full_adder_4_co, full_adder_4_s, full_adder_5_co, full_adder_5_s,
       full_adder_6_co, full_adder_6_s, full_adder_7_co, full_adder_7_s, full_adder_8_co, full_adder_8_s,
       not_1_out, xor_1_out;

  xor xor_1 (xor_1_out, full_adder_1_co, C);
  Full_Adder full_adder_1 (.X(X0), .Y(Y0), .C(full_adder_2_co), .S(full_adder_1_s), .CO(full_adder_1_co));
  Full_Adder full_adder_2 (.X(X1), .Y(Y1), .C(full_adder_3_co), .S(full_adder_2_s), .CO(full_adder_2_co));
  Full_Adder full_adder_3 (.X(X2), .Y(Y2), .C(full_adder_4_co), .S(full_adder_3_s), .CO(full_adder_3_co));
  Full_Adder full_adder_4 (.X(X3), .Y(Y3), .C(full_adder_5_co), .S(full_adder_4_s), .CO(full_adder_4_co));
  Full_Adder full_adder_5 (.X(X4), .Y(Y4), .C(full_adder_6_co), .S(full_adder_5_s), .CO(full_adder_5_co));
  Full_Adder full_adder_6 (.X(X5), .Y(Y5), .C(full_adder_7_co), .S(full_adder_6_s), .CO(full_adder_6_co));
  Full_Adder full_adder_7 (.X(X6), .Y(Y6), .C(full_adder_8_co), .S(full_adder_7_s), .CO(full_adder_7_co));
  Full_Adder full_adder_8 (.X(X7), .Y(Y7), .C(C), .S(full_adder_8_s), .CO(full_adder_8_co));
  not not_1 (not_1_out, S);
  and and_1 (and_1_out, full_adder_1_co, not_1_out);
  and and_2 (and_2_out, xor_1_out, S);
  assign O0 = E ? full_adder_1_s : 1'bz;  // Driver driver_1
  assign O1 = E ? full_adder_2_s : 1'bz;  // Driver driver_2
  assign O2 = E ? full_adder_3_s : 1'bz;  // Driver driver_3
  assign O3 = E ? full_adder_4_s : 1'bz;  // Driver driver_4
  assign O4 = E ? full_adder_5_s : 1'bz;  // Driver driver_5
  assign O5 = E ? full_adder_6_s : 1'bz;  // Driver driver_6
  assign O6 = E ? full_adder_7_s : 1'bz;  // Driver driver_7
  assign O7 = E ? full_adder_8_s : 1'bz;  // Driver driver_8
  assign CO = E ? and_1_out : 1'bz;  // Driver driver_9
  assign OO = E ? and_2_out : 1'bz;  // Driver driver_10
endmodule
