// Digital circuit Multiplier8b.dig as structural Verilog
module Multiplier8b (
  input  E,
  input  X0,
  input  X1,
  input  X2,
  input  X3,
  input  X4,
  input  X5,
  input  X6,
  input  X7,
  input  Y0,
  input  Y1,
  input  Y2,
  input  Y3,
  input  Y4,
  input  Y5,
  input  Y6,
  input  Y7,
  output O0,
  output O1,
  output O2,
  output O3,
  output O4,
  output O5,
  output O6,
  output O7,
  output O8,
  output O9,
  output O10,
  output O11,
  output O12,
  output O13,
  output O14,
  output O15,
  output F0
);

  wire adder8b_1_p12, adder8b_1_p14, adder8b_1_p16, adder8b_1_p18, adder8b_1_p20, adder8b_1_p22,
       adder8b_1_p24, adder8b_1_p26, adder8b_1_p28, adder8b_2_p13, adder8b_2_p14, adder8b_2_p15,
       adder8b_2_p16, adder8b_2_p17, adder8b_2_p18, adder8b_2_p19, adder8b_2_p20, adder8b_2_p21,
       adder8b_2_p22, adder8b_2_p23, adder8b_2_p24, adder8b_2_p25, adder8b_2_p26, and_1_out,
       collectiveand8b_1_o0, collectiveand8b_1_o1, collectiveand8b_1_o2, collectiveand8b_1_o3,
       collectiveand8b_1_o4, collectiveand8b_1_o5, collectiveand8b_1_o6, collectiveand8b_1_o7,
       collectiveand8b_2_o0, collectiveand8b_2_o1, collectiveand8b_2_o2, collectiveand8b_2_o3,
       collectiveand8b_2_o4, collectiveand8b_2_o5, collectiveand8b_2_o6, collectiveand8b_2_o7,
       notconnected_1_out;

  CollectiveAnd8b collectiveand8b_1 (
    .AND(Y1), .O0(collectiveand8b_1_o0), .O1(collectiveand8b_1_o1), .O2(collectiveand8b_1_o2),
    .O3(collectiveand8b_1_o3), .O4(collectiveand8b_1_o4), .O5(collectiveand8b_1_o5),
    .O6(collectiveand8b_1_o6), .O7(collectiveand8b_1_o7));  // open: I0, I1, I2, I3, I4, I5, I6, I7
  // NotConnected on notconnected_1_out
  CollectiveAnd8b collectiveand8b_2 (
    .I0(X0), .I1(X1), .I2(X2), .I3(X3), .I4(X4), .I5(X5), .I6(X6), .I7(X7), .AND(Y0),
    .O0(collectiveand8b_2_o0), .O1(collectiveand8b_2_o1), .O2(collectiveand8b_2_o2),
    .O3(collectiveand8b_2_o3), .O4(collectiveand8b_2_o4), .O5(collectiveand8b_2_o5),
    .O6(collectiveand8b_2_o6), .O7(collectiveand8b_2_o7));
  and and_1 (and_1_out, X0, Y0);
  // Adder8b adder8b_1: pin names not known; wires that end beside it: 1'b0, collectiveand8b_1_o7, collectiveand8b_1_o6, collectiveand8b_1_o5, collectiveand8b_1_o4, collectiveand8b_1_o3, collectiveand8b_1_o2, collectiveand8b_1_o1, collectiveand8b_1_o0, notconnected_1_out, collectiveand8b_2_o7, adder8b_1_p12, collectiveand8b_2_o6, adder8b_1_p14, collectiveand8b_2_o5, adder8b_1_p16, collectiveand8b_2_o4, adder8b_1_p18, collectiveand8b_2_o3, adder8b_1_p20, collectiveand8b_2_o2, adder8b_1_p22, collectiveand8b_2_o1, adder8b_1_p24, collectiveand8b_2_o0, adder8b_1_p26, 1'b1, adder8b_1_p28, F0
  // Adder8b adder8b_2: pin names not known; wires that end beside it: X3, X2, X1, X0, adder8b_1_p12, adder8b_1_p14, adder8b_1_p16, adder8b_1_p18, adder8b_1_p20, adder8b_1_p22, adder8b_1_p24, adder8b_1_p26, adder8b_2_p13, adder8b_2_p14, adder8b_2_p15, adder8b_2_p16, adder8b_2_p17, adder8b_2_p18, adder8b_2_p19, adder8b_2_p20, adder8b_2_p21, adder8b_2_p22, adder8b_2_p23, adder8b_2_p24, adder8b_2_p25, adder8b_2_p26, adder8b_2_p13, adder8b_1_p28, and_1_out
  assign O0 = E ? and_1_out : 1'bz;  // Driver driver_1
  assign O1 = E ? adder8b_1_p28 : 1'bz;  // Driver driver_2
  assign O2 = E ? adder8b_2_p13 : 1'bz;  // Driver driver_3
  assign O3 = E ? adder8b_2_p26 : 1'bz;  // Driver driver_4
  assign O4 = E ? adder8b_2_p25 : 1'bz;  // Driver driver_5
  assign O5 = E ? adder8b_2_p24 : 1'bz;  // Driver driver_6
  assign O6 = E ? adder8b_2_p23 : 1'bz;  // Driver driver_7
  assign O7 = E ? adder8b_2_p22 : 1'bz;  // Driver driver_8
  assign O8 = E ? adder8b_2_p21 : 1'bz;  // Driver driver_9
  assign O9 = E ? adder8b_2_p20 : 1'bz;  // Driver driver_10
  assign O10 = E ? adder8b_2_p19 : 1'bz;  // Driver driver_11
  assign O11 = E ? adder8b_2_p18 : 1'bz;  // Driver driver_12
  assign O12 = E ? adder8b_2_p17 : 1'bz;  // Driver driver_13
  assign O13 = E ? adder8b_2_p16 : 1'bz;  // Driver driver_14
  assign O14 = E ? adder8b_2_p15 : 1'bz;  // Driver driver_15
  assign O15 = E ? adder8b_2_p14 : 1'bz;  // Driver driver_16
endmodule
