// Digital circuit Clock.dig as structural Verilog
module Clock (
  input  HLT,
  input  Clock,
  input  M_CLK,
  input  M_E,
  output CLK
);

  wire and_1_out, and_2_out, not_1_out, not_2_out;

  not not_1 (not_1_out, HLT);
  not not_2 (not_2_out, M_E);
  and and_1 (and_1_out, not_1_out, not_2_out, Clock);
  and and_2 (and_2_out, M_CLK, M_E);
  or or_1 (CLK, and_1_out, and_2_out);
endmodule
