// Digital circuit IOHandler.dig as structural Verilog
module IOHandler (
  input  D0,
  input  D1,
  input  D2,
  input  D3,
  input  D4,
  input  D5,
  input  D6,
  input  D7,
  input  A0,
  input  A1,
  input  A2,
  input  A3,
  input  A4,
  input  A5,
  input  A6,
  input  A7
);

  Register register_1 ();  // open: CLK, E, R, W, D0, D1, D2, D3, D4, D5, D6, D7, O0, O1, O2, O3, O4, O5, O6, O7
  Register register_2 ();  // open: CLK, E, R, W, D0, D1, D2, D3, D4, D5, D6, D7, O0, O1, O2, O3, O4, O5, O6, O7
endmodule
