// Digital circuit Instruction Decoder.dig as structural Verilog
module Instruction_Decoder (
  input  CLK,
  input  I0,
  input  I1,
  input  I2,
  input  I3,
  input  I4,
  input  I5,
  input  I6,
  input  I7,
  input  IRQ,
  input  INT,
  input  F0,
  input  FC,
  input  FO,
  input  FN,
  output D0,
  output D1,
  output D2,
  output D3,
  output D4,
  output D5,
  output D6,
  output D7,
  output ALUE,
  output ALU_B,
  output ALUC,
  output ALUADD,
  output ALUAND,
  output ALUOR,
  output ALUNOT,
  output ALUXOR,
  output ALUSL,
  output ALUSR,
  output ALURL,
  output ALURR,
  output AR,
  output AW,
  output XR,
  output XW,
  output YR,
  output YW,
  output ZR,
  output ZW,
  output PCE,
  output PCHR,
  output PCHW,
  output PCLR,
  output PCLW,
  output SPR,
  output SPW,
  output SPINC,
  output SPDEC,
  output LHR,
  output LHW,
  output LLR,
  output LLW,
  output MALW,
  output MAHW,
  output INTACK,
  output HLT,
  output MR,
  output MW,
  output DBOUT,
  output DBIN,
  output TW,
  output MAINC
);

  wire and_1_out, flagregister_1_o0, flagsregister4b_1_o0, flagsregister4b_1_o1, flagsregister4b_1_o2,
       flagsregister4b_1_o3, interrupthandler_1_blkinst, lookuptable_1_out, not_1_out, not_2_out, not_3_out,
       or_1_out, or_2_out, or_3_out, or_4_out, or_5_out, or_6_out, or_7_out, or_8_out, reset_1_out, xor_1_out;
  wire [10:0] counter_1_out;
  wire [60:2] interrupthandler_1_inst;

  or or_1 (or_1_out, reset_1_out, CLK);
  or or_2 (or_2_out, or_8_out, ~reset_1_out);  // Or
  Reset reset_1 (.out(reset_1_out));
  or or_3 (or_3_out, I0, FC);
  or or_4 (or_4_out, I1, FN);
  or or_5 (or_5_out, I2, F0);
  or or_6 (or_6_out, I3, FO);
  not not_1 (not_1_out, or_1_out);
  Counter #(.Bits(3)) counter_1 (.en(not_1_out), .C(not_1_out), .clr(or_2_out), .out(counter_1_out[2:0]));  // open: ovf
  not not_2 (not_2_out, or_1_out);
  Register I (
    .CLK(or_1_out), .E(1'b1), .R(1'b1), .W(interrupthandler_1_inst[35]), .D0(I0), .D1(I1), .D2(I2), .D3(I3),
    .D4(I4), .D5(I5), .D6(I6), .D7(I7), .O0(counter_1_out[3]), .O1(counter_1_out[4]), .O2(counter_1_out[5]),
    .O3(counter_1_out[6]), .O4(counter_1_out[7]), .O5(counter_1_out[8]), .O6(counter_1_out[9]),
    .O7(counter_1_out[10]));
  FlagsRegister4b flagsregister4b_1 (
    .CLK(not_2_out), .F0(or_3_out), .S0(interrupthandler_1_inst[39]), .R0(interrupthandler_1_inst[38]),
    .E0(interrupthandler_1_inst[40]), .F1(or_4_out), .S1(1'b0), .R1(1'b0), .E1(interrupthandler_1_inst[42]),
    .F2(or_5_out), .S2(1'b0), .R2(1'b0), .E2(interrupthandler_1_inst[43]), .F3(or_6_out), .S3(1'b0),
    .R3(1'b0), .E3(interrupthandler_1_inst[44]), .O0(flagsregister4b_1_o0), .O1(flagsregister4b_1_o1),
    .O2(flagsregister4b_1_o2), .O3(flagsregister4b_1_o3));
  FlagRegister flagregister_1 (
    .CLK(not_2_out), .F0(I4), .S0(interrupthandler_1_inst[46]), .R0(interrupthandler_1_inst[45]),
    .E0(interrupthandler_1_inst[47]), .O0(flagregister_1_o0));
  InterruptHandler interrupthandler_1 (
    .S0(counter_1_out[0]), .S1(counter_1_out[1]), .S2(counter_1_out[2]), .INT(INT), .IRQ(or_7_out),
    .IMF(flagregister_1_o0), .INTACK(INTACK), .BLKINST(interrupthandler_1_blkinst),
    .INST({MAINC, interrupthandler_1_inst[60], TW, interrupthandler_1_inst[58:55], DBIN, DBOUT, interrupthandler_1_inst[52], HLT, INTACK, interrupthandler_1_inst[49:38], MW, MR, interrupthandler_1_inst[35], MAHW, MALW, LLW, LLR, LHW, LHR, SPDEC, SPINC, SPW, SPR, PCLW, PCLR, PCHW, PCHR, PCE, ZW, ZR, YW, YR, XW, XR, AW, AR, ALURR, ALURL, ALUSR, ALUSL, ALUXOR, ALUNOT, ALUOR, ALUAND, ALUADD, interrupthandler_1_inst[2], ALU_B, ALUE}),
    .D0(D0), .D1(D1), .D2(D2), .D3(D3), .D4(D4), .D5(D5), .D6(D6), .D7(D7));
  or or_7 (or_7_out, interrupthandler_1_inst[49], IRQ);
  ROM #(.AddrBits(11), .Bits(62)) rom_1 (
    .A(counter_1_out), .sel(not_3_out),
    .D({MAINC, interrupthandler_1_inst[60], TW, interrupthandler_1_inst[58:55], DBIN, DBOUT, interrupthandler_1_inst[52], HLT, INTACK, interrupthandler_1_inst[49:38], MW, MR, interrupthandler_1_inst[35], MAHW, MALW, LLW, LLR, LHW, LHR, SPDEC, SPINC, SPW, SPR, PCLW, PCLR, PCHW, PCHR, PCE, ZW, ZR, YW, YR, XW, XR, AW, AR, ALURR, ALURL, ALUSR, ALUSL, ALUXOR, ALUNOT, ALUOR, ALUAND, ALUADD, interrupthandler_1_inst[2], ALU_B, ALUE}));
  not not_3 (not_3_out, interrupthandler_1_blkinst);
  PinControl8b pincontrol8b_1 (
    .E(interrupthandler_1_inst[48]), .D0(flagsregister4b_1_o3), .D1(flagsregister4b_1_o2),
    .D2(flagsregister4b_1_o1), .D3(flagsregister4b_1_o0), .D4(flagregister_1_o0), .D5(1'b0), .D6(1'b0),
    .D7(1'b0), .O0(D0), .O1(D1), .O2(D2), .O3(D3), .O4(D4), .O5(D5), .O6(D6), .O7(D7));
  PinControl8b pincontrol8b_2 (
    .E(interrupthandler_1_inst[60]), .D0(1'b0), .D1(1'b0), .D2(1'b0), .D3(1'b0), .D4(1'b0), .D5(1'b0),
    .D6(1'b0), .D7(interrupthandler_1_inst[41]), .O0(D0), .O1(D1), .O2(D2), .O3(D3), .O4(D4), .O5(D5),
    .O6(D6), .O7(D7));
  LookUpTable lookuptable_1 (
    .in0(interrupthandler_1_inst[56]), .in1(interrupthandler_1_inst[57]), .in2(flagsregister4b_1_o0),
    .in3(flagsregister4b_1_o1), .in4(flagsregister4b_1_o2), .in5(flagsregister4b_1_o3),
    .out(lookuptable_1_out));
  xor xor_1 (xor_1_out, interrupthandler_1_inst[55], lookuptable_1_out);
  and and_1 (and_1_out, xor_1_out, interrupthandler_1_inst[58]);
  or or_8 (or_8_out, interrupthandler_1_inst[52], and_1_out);
  assign ALUC = ~interrupthandler_1_inst[41] ? interrupthandler_1_inst[2] : 1'bz;  // DriverInvSel driverinvsel_1
  assign ALUC = interrupthandler_1_inst[41] ? flagsregister4b_1_o0 : 1'bz;  // Driver driver_1

  // Notes on the sheet:
  //   IW
  //   IMF E/S/R
  //   VF E
  //   ZF E
  //   NF E
  //   CF E/S/R
  //   SCF
  //   CCF
  //   ECF
  //   ENF
  //   EZF
  //   EVF
  //   SIMF
  //   CIMF
  //   EIMF
  //   FTB
  //   CC
  //   ALU
  //   Reg
  //   MEM
  //   F/INT
  //   MISC
  //   contents of lookuptable_1 (hex, n*v repeats v):
  //   a,0,0,0,1,0,0,0,a,1,a,0,1,1,0,0,0,0,1,0,1,0,1,0,0,1,1,0,1,1,1,0,0,a,0,1,1,0,0,1,0,
  //   1,0,1,1,1,0,1,0,0,1,1,1,0,1,1,0,1,1,1,1,1,1,1
  //   IRQ
  //   SCF
  //   CCF
  //   ECF
  //   OCF
  //   ENF
  //   EZF
  //   EVF
  //   SIMF
  //   CIMF
  //   EIMF
endmodule
