// Digital circuit InterruptHandler.dig as structural Verilog
module InterruptHandler (
  input  S0,
  input  S1,
  input  S2,
  input  INT,
  input  IRQ,
  input  IMF,
  input  INTACK,
  output BLKINST,
  output [61:0] INST,
  output D0,
  output D1,
  output D2,
  output D3,
  output D4,
  output D5,
  output D6,
  output D7
);

  wire and_1_out, and_2_out, and_3_out, and_4_out, and_5_out, and_6_out, or_1_out, or_2_out, reset_1_out;
  wire [63:0] rom_1_d;
  wire [63:62] driver_1_out;

  and and_1 (and_1_out, IRQ, ~IMF);  // And
  or or_1 (or_1_out, INT, and_1_out);
  and and_2 (and_2_out, ~INT, and_1_out);  // And
  and and_3 (and_3_out, ~S0, ~S1, ~S2);  // And
  and and_4 (and_4_out, and_3_out, or_1_out);
  or or_2 (or_2_out, INTACK, reset_1_out);
  Reset #(.invertOutput("false")) reset_1 (.out(reset_1_out));
  RS_FF_AS rs_ff_as_1 (.S(and_4_out), .R(or_2_out), .Q(BLKINST));  // open: nQ
  ROM #(.AddrBits(3), .Bits(64)) rom_1 (.A({S2, S1, S0}), .sel(BLKINST), .D(rom_1_d));
  assign {driver_1_out, INST} = BLKINST ? rom_1_d : 64'bz;  // Driver driver_1
  assign {driver_1_out, INST} = ~BLKINST ? {64{1'b0}} : 64'bz;  // DriverInvSel driverinvsel_1
  and and_5 (and_5_out, driver_1_out[63], INT);
  and and_6 (and_6_out, driver_1_out[63], and_2_out);
  PinControl8b pincontrol8b_1 (
    .E(driver_1_out[62]), .D0(1'b1), .D1(1'b1), .D2(1'b1), .D3(1'b1), .D4(1'b1), .D5(1'b1), .D6(1'b1),
    .D7(1'b1), .O0(D0), .O1(D1), .O2(D2), .O3(D3), .O4(D4), .O5(D5), .O6(D6), .O7(D7));
  PinControl8b pincontrol8b_2 (
    .E(and_5_out), .D0(1'b1), .D1(1'b1), .D2(1'b1), .D3(1'b1), .D4(1'b1), .D5(1'b1), .D6(1'b1), .D7(1'b0),
    .O0(D0), .O1(D1), .O2(D2), .O3(D3), .O4(D4), .O5(D5), .O6(D6), .O7(D7));
  PinControl8b pincontrol8b_3 (
    .E(and_6_out), .D0(1'b1), .D1(1'b1), .D2(1'b1), .D3(1'b1), .D4(1'b1), .D5(1'b1), .D6(1'b0), .D7(1'b0),
    .O0(D0), .O1(D1), .O2(D2), .O3(D3), .O4(D4), .O5(D5), .O6(D6), .O7(D7));
endmodule
