// Digital circuit ProgramCounter16.dig as structural Verilog
module ProgramCounter16 (
  input  CLK,
  input  E,
  input  RL,
  input  WL,
  input  RH,
  input  WH,
  input  D0,
  input  D1,
  input  D2,
  input  D3,
  input  D4,
  input  D5,
  input  D6,
  input  D7,
  output O0,
  output O1,
  output O2,
  output O3,
  output O4,
  output O5,
  output O6,
  output O7
);

  wire incrementer8b_1_co, or_1_out, or_2_out, or_3_out, or_4_out, pincontrol8b_1_o0, pincontrol8b_1_o1,
       pincontrol8b_1_o2, pincontrol8b_1_o3, pincontrol8b_1_o4, pincontrol8b_1_o5, pincontrol8b_1_o6,
       pincontrol8b_1_o7, pincontrol8b_2_o0, pincontrol8b_2_o1, pincontrol8b_2_o2, pincontrol8b_2_o3,
       pincontrol8b_2_o4, pincontrol8b_2_o5, pincontrol8b_2_o6, pincontrol8b_2_o7, register_1_o0,
       register_1_o1, register_1_o2, register_1_o3, register_1_o4, register_1_o5, register_1_o6,
       register_1_o7, register_2_o0, register_2_o1, register_2_o2, register_2_o3, register_2_o4,
       register_2_o5, register_2_o6, register_2_o7;

  PinControl8b pincontrol8b_1 (
    .E(WL), .D0(D0), .D1(D1), .D2(D2), .D3(D3), .D4(D4), .D5(D5), .D6(D6), .D7(D7), .O0(pincontrol8b_1_o0),
    .O1(pincontrol8b_1_o1), .O2(pincontrol8b_1_o2), .O3(pincontrol8b_1_o3), .O4(pincontrol8b_1_o4),
    .O5(pincontrol8b_1_o5), .O6(pincontrol8b_1_o6), .O7(pincontrol8b_1_o7));
  PinControl8b pincontrol8b_2 (
    .E(WH), .D0(D0), .D1(D1), .D2(D2), .D3(D3), .D4(D4), .D5(D5), .D6(D6), .D7(D7), .O0(pincontrol8b_2_o0),
    .O1(pincontrol8b_2_o1), .O2(pincontrol8b_2_o2), .O3(pincontrol8b_2_o3), .O4(pincontrol8b_2_o4),
    .O5(pincontrol8b_2_o5), .O6(pincontrol8b_2_o6), .O7(pincontrol8b_2_o7));
  or or_1 (or_1_out, E, RL);
  or or_2 (or_2_out, WL, E);
  or or_3 (or_3_out, E, RH);
  or or_4 (or_4_out, WH, E);
  Register register_1 (
    .CLK(CLK), .E(1'b1), .R(or_1_out), .W(or_2_out), .D0(pincontrol8b_1_o0), .D1(pincontrol8b_1_o1),
    .D2(pincontrol8b_1_o2), .D3(pincontrol8b_1_o3), .D4(pincontrol8b_1_o4), .D5(pincontrol8b_1_o5),
    .D6(pincontrol8b_1_o6), .D7(pincontrol8b_1_o7), .O0(register_1_o0), .O1(register_1_o1),
    .O2(register_1_o2), .O3(register_1_o3), .O4(register_1_o4), .O5(register_1_o5), .O6(register_1_o6),
    .O7(register_1_o7));
  Register register_2 (
    .CLK(CLK), .E(1'b1), .R(or_3_out), .W(or_4_out), .D0(pincontrol8b_2_o0), .D1(pincontrol8b_2_o1),
    .D2(pincontrol8b_2_o2), .D3(pincontrol8b_2_o3), .D4(pincontrol8b_2_o4), .D5(pincontrol8b_2_o5),
    .D6(pincontrol8b_2_o6), .D7(pincontrol8b_2_o7), .O0(register_2_o0), .O1(register_2_o1),
    .O2(register_2_o2), .O3(register_2_o3), .O4(register_2_o4), .O5(register_2_o5), .O6(register_2_o6),
    .O7(register_2_o7));
  PinControl8b pincontrol8b_3 (
    .E(RL), .D0(register_1_o0), .D1(register_1_o1), .D2(register_1_o2), .D3(register_1_o3),
    .D4(register_1_o4), .D5(register_1_o5), .D6(register_1_o6), .D7(register_1_o7), .O0(O0), .O1(O1),
    .O2(O2), .O3(O3), .O4(O4), .O5(O5), .O6(O6), .O7(O7));
  PinControl8b pincontrol8b_4 (
    .E(RH), .D0(register_2_o0), .D1(register_2_o1), .D2(register_2_o2), .D3(register_2_o3),
    .D4(register_2_o4), .D5(register_2_o5), .D6(register_2_o6), .D7(register_2_o7), .O0(O0), .O1(O1),
    .O2(O2), .O3(O3), .O4(O4), .O5(O5), .O6(O6), .O7(O7));
  Incrementer8b incrementer8b_1 (
    .E(E), .D0(register_1_o0), .D1(register_1_o1), .D2(register_1_o2), .D3(register_1_o3),
    .D4(register_1_o4), .D5(register_1_o5), .D6(register_1_o6), .D7(register_1_o7), .INC(E),
    .O0(pincontrol8b_1_o0), .O1(pincontrol8b_1_o1), .O2(pincontrol8b_1_o2), .O3(pincontrol8b_1_o3),
    .O4(pincontrol8b_1_o4), .O5(pincontrol8b_1_o5), .O6(pincontrol8b_1_o6), .O7(pincontrol8b_1_o7),
    .CO(incrementer8b_1_co));
  Incrementer8b incrementer8b_2 (
    .E(E), .D0(register_2_o0), .D1(register_2_o1), .D2(register_2_o2), .D3(register_2_o3),
    .D4(register_2_o4), .D5(register_2_o5), .D6(register_2_o6), .D7(register_2_o7), .INC(incrementer8b_1_co),
    .O0(pincontrol8b_2_o0), .O1(pincontrol8b_2_o1), .O2(pincontrol8b_2_o2), .O3(pincontrol8b_2_o3),
    .O4(pincontrol8b_2_o4), .O5(pincontrol8b_2_o5), .O6(pincontrol8b_2_o6), .O7(pincontrol8b_2_o7));  // open: CO
endmodule
